// Logisim project mips.circ as structural Verilog: 8 circuits, main circuit main
module IF_ID (
  input  [31:0] Instr_IF,
  input  [31:0] PC4_IF,
  input  in_3,
  input  clk,
  output [31:0] Instr_ID,
  output [31:0] PC4_ID
);

  Register #(.width(32)) register_1 (.D(Instr_IF), .en(1'b1), .clk(clk), .Q(Instr_ID), .clr(in_3));
  Register #(.width(32)) register_2 (.D(PC4_IF), .en(1'b1), .clk(clk), .Q(PC4_ID), .clr(in_3));
endmodule

module main (
  input  [3:0] in_1
);

  wire alu_1_zero, and_1_out, clock_1_out, control_1_alusrc, control_1_branch, control_1_memread,
       control_1_memtoreg, control_1_memwrite, control_1_regdst, control_1_regwrite,
       ex_mem_1_branchtaken_exmem, ex_mem_1_memread_exmem, ex_mem_1_memtoreg_exmem, ex_mem_1_memwrite_exmem,
       ex_mem_1_regwrite_exmem, id_ex_1_alusrc_out, id_ex_1_branch_out, mem_wb_1_memtoreg_out,
       mem_wb_1_regwrite_out;
  wire [1:0] control_1_aluop;
  wire [4:0] bit_extender_3_out, ex_mem_1_writereg_exmem, mem_wb_1_writereg_out;
  wire [15:0] bit_extender_1_out, bit_extender_4_out;
  wire [31:0] adder_1_out, adder_2_out, alu_1_result, bit_extender_2_out, ex_mem_1_aluresult_exmem,
       ex_mem_1_branchtarget_exmem, ex_mem_1_writedata_exmem, id_ex_1_imm_out, id_ex_1_pc_out,
       id_ex_1_rd1_out, id_ex_1_rd2_out, if_id_1_instr_id, if_id_1_pc4_id, mem_wb_1_aluresult_out,
       mem_wb_1_readdata_out, multiplexer_1_out, multiplexer_2_out, multiplexer_3_out, ram_1_dout,
       register_1_q, registers_1_readdata1, registers_1_readdata2, rom_1_data, shifter_1_out;

  Clock clock_1 (.out(clock_1_out));
  Register #(.width(32)) register_1 (.D(multiplexer_1_out), .en(1'b1), .clk(clock_1_out), .Q(register_1_q), .clr(1'b0));
  Adder #(.width(32)) adder_1 (.a(register_1_q), .b(32'h4), .out(adder_1_out));  // open: cin, cout
  ROM #(.addrWidth(16), .dataWidth(32)) rom_1 (.addr(bit_extender_1_out), .data(rom_1_data));
  Bit_Extender #(.in_width(32)) bit_extender_1 (.in(register_1_q), .out(bit_extender_1_out));
  Multiplexer #(.width(32)) multiplexer_1 (
    .in0(adder_1_out), .in1(ex_mem_1_branchtarget_exmem), .out(multiplexer_1_out),
    .sel(ex_mem_1_branchtaken_exmem));
  IF_ID if_id_1 (
    .Instr_IF(rom_1_data), .PC4_IF(adder_1_out), .in_3(1'b0), .clk(clock_1_out), .Instr_ID(if_id_1_instr_id),
    .PC4_ID(if_id_1_pc4_id));
  assign bit_extender_2_out = {{16{if_id_1_instr_id[15]}}, if_id_1_instr_id[15:0]};  // Bit_Extender bit_extender_2
  Control control_1 (
    .Opcode(if_id_1_instr_id[31:26]), .RegDst(control_1_regdst), .ALUSrc(control_1_alusrc),
    .ALUOp(control_1_aluop), .MemRead(control_1_memread), .MemWrite(control_1_memwrite),
    .MemToReg(control_1_memtoreg), .RegWrite(control_1_regwrite), .Branch(control_1_branch));
  Registers registers_1 (
    .RegWrite(mem_wb_1_regwrite_out), .rd(mem_wb_1_writereg_out), .rs(if_id_1_instr_id[25:21]),
    .rt(if_id_1_instr_id[20:16]), .WriteData(multiplexer_3_out), .clk(clock_1_out),
    .ReadData1(registers_1_readdata1), .ReadData2(registers_1_readdata2));
  ID_EX id_ex_1 (
    .pc_in(if_id_1_pc4_id), .RD1_in(registers_1_readdata1), .RD2_in(registers_1_readdata2),
    .Imm_in(bit_extender_2_out), .stall(1'b1), .flush(1'b0), .rs_in(if_id_1_instr_id[25:21]),
    .rt_in(if_id_1_instr_id[20:16]), .rd_in(if_id_1_instr_id[15:11]), .regdst_in(control_1_regdst),
    .ALUsrec_in(control_1_alusrc), .ALUOp_in(control_1_aluop), .Branch_in(control_1_branch),
    .clk(clock_1_out), .pc_out(id_ex_1_pc_out), .RD1_out(id_ex_1_rd1_out), .RD2_out(id_ex_1_rd2_out),
    .Imm_out(id_ex_1_imm_out), .ALUsrc_out(id_ex_1_alusrc_out), .Branch_out(id_ex_1_branch_out));  // open: rs_out, rt_out, rd_out, REGDST_out, ALUOP_out
  Multiplexer #(.width(32)) multiplexer_2 (
    .in0(id_ex_1_rd2_out), .in1(id_ex_1_imm_out), .out(multiplexer_2_out), .sel(id_ex_1_alusrc_out));
  Bit_Extender #(.in_width(32), .out_width(5)) bit_extender_3 (.in(id_ex_1_rd1_out), .out(bit_extender_3_out));
  Shifter #(.width(32)) shifter_1 (.in(id_ex_1_imm_out), .\dist (5'b00010), .out(shifter_1_out));
  Adder #(.width(32)) adder_2 (.a(id_ex_1_pc_out), .b(shifter_1_out), .out(adder_2_out));  // open: cin, cout
  ALU alu_1 (.A(id_ex_1_rd1_out), .B(multiplexer_2_out), .ALUCtrl(in_1), .Result(alu_1_result), .Zero(alu_1_zero));
  and and_1 (and_1_out, alu_1_zero, id_ex_1_branch_out);
  EX_MEM ex_mem_1 (
    .ALUResult_EX(alu_1_result), .WriteData_EX(id_ex_1_rd2_out), .BranchTaken_EX(and_1_out),
    .MemRead_EX(control_1_memread), .MemWrite_EX(control_1_memwrite), .MemToReg_EX(control_1_memtoreg),
    .RegWrite_EX(control_1_regwrite), .BranchTarget_EX(adder_2_out), .WriteReg_EX(bit_extender_3_out),
    .reset(1'b0), .clk(clock_1_out), .ALUResult_EXMEM(ex_mem_1_aluresult_exmem),
    .WriteData_EXMEM(ex_mem_1_writedata_exmem), .BranchTaken_EXMEM(ex_mem_1_branchtaken_exmem),
    .MemRead_EXMEM(ex_mem_1_memread_exmem), .MemWrite_EXMEM(ex_mem_1_memwrite_exmem),
    .MemToReg_EXMEM(ex_mem_1_memtoreg_exmem), .RegWrite_EXMEM(ex_mem_1_regwrite_exmem),
    .BranchTarget_EXMEM(ex_mem_1_branchtarget_exmem), .WriteReg_EXMEM(ex_mem_1_writereg_exmem));
  Bit_Extender #(.in_width(32)) bit_extender_4 (.in(ex_mem_1_aluresult_exmem), .out(bit_extender_4_out));
  RAM #(.addrWidth(16), .dataWidth(32)) ram_1 (
    .addr(bit_extender_4_out), .we(ex_mem_1_memwrite_exmem), .oe(ex_mem_1_memread_exmem), .clk(clock_1_out),
    .din(ex_mem_1_writedata_exmem), .dout(ram_1_dout));
  MEM_WB mem_wb_1 (
    .ReadData_in(ram_1_dout), .ALUResult_in(ex_mem_1_aluresult_exmem), .WriteReg_in(ex_mem_1_writereg_exmem),
    .RegWrite_in(ex_mem_1_regwrite_exmem), .MemToReg_in(ex_mem_1_memtoreg_exmem), .reset(1'b0),
    .clk(clock_1_out), .ReadData_out(mem_wb_1_readdata_out), .ALUResult_out(mem_wb_1_aluresult_out),
    .WriteReg_out(mem_wb_1_writereg_out), .RegWrite_out(mem_wb_1_regwrite_out),
    .MemToReg_out(mem_wb_1_memtoreg_out));
  Multiplexer #(.width(32)) multiplexer_3 (
    .in0(mem_wb_1_aluresult_out), .in1(mem_wb_1_readdata_out), .out(multiplexer_3_out),
    .sel(mem_wb_1_memtoreg_out));
endmodule

module Registers (
  input  RegWrite,
  input  [4:0] rd,
  input  [4:0] rs,
  input  [4:0] rt,
  input  [31:0] WriteData,
  input  clk,
  output [31:0] ReadData1,
  output [31:0] ReadData2
);

  wire decoder_1_out0, decoder_1_out1, decoder_1_out2, decoder_1_out3, decoder_1_out4, decoder_1_out5,
       decoder_1_out6, decoder_1_out7, decoder_1_out8, decoder_1_out9, decoder_1_out10, decoder_1_out11,
       decoder_1_out12, decoder_1_out13, decoder_1_out14, decoder_1_out15, decoder_1_out16, decoder_1_out17,
       decoder_1_out18, decoder_1_out19, decoder_1_out20, decoder_1_out21, decoder_1_out22, decoder_1_out23,
       decoder_1_out24, decoder_1_out25, decoder_1_out26, decoder_1_out27, decoder_1_out28, decoder_1_out29,
       decoder_1_out30, decoder_1_out31;
  wire [31:0] R0_q, R1_q, R2_q, R3_q, R4_q, R5_q, R6_q, R7_q, R8_q, R9_q, R10_q, R11_q, R12_q, R13_q, R14_q,
       R15_q, R16_q, R17_q, R18_q, R19_q, R20_q, R21_q, R22_q, R23_q, R24_q, R25_q, R26_q, R27_q, R28_q,
       R29_q, R30_q, R31_q;

  Decoder #(.select(5)) decoder_1 (
    .out0(decoder_1_out0), .out1(decoder_1_out1), .out2(decoder_1_out2), .out3(decoder_1_out3),
    .out4(decoder_1_out4), .out5(decoder_1_out5), .out6(decoder_1_out6), .out7(decoder_1_out7),
    .out8(decoder_1_out8), .out9(decoder_1_out9), .out10(decoder_1_out10), .out11(decoder_1_out11),
    .out12(decoder_1_out12), .out13(decoder_1_out13), .out14(decoder_1_out14), .out15(decoder_1_out15),
    .out16(decoder_1_out16), .out17(decoder_1_out17), .out18(decoder_1_out18), .out19(decoder_1_out19),
    .out20(decoder_1_out20), .out21(decoder_1_out21), .out22(decoder_1_out22), .out23(decoder_1_out23),
    .out24(decoder_1_out24), .out25(decoder_1_out25), .out26(decoder_1_out26), .out27(decoder_1_out27),
    .out28(decoder_1_out28), .out29(decoder_1_out29), .out30(decoder_1_out30), .out31(decoder_1_out31),
    .en(RegWrite));  // open: sel
  Register #(.width(32)) R4 (.D(WriteData), .en(decoder_1_out4), .clk(clk), .Q(R4_q));  // open: clr
  Register #(.width(32)) R9 (.D(WriteData), .en(decoder_1_out9), .clk(clk), .Q(R9_q));  // open: clr
  Register #(.width(32)) R14 (.D(WriteData), .en(decoder_1_out14), .clk(clk), .Q(R14_q));  // open: clr
  Register #(.width(32)) R19 (.D(WriteData), .en(decoder_1_out19), .clk(clk), .Q(R19_q));  // open: clr
  Register #(.width(32)) R24 (.D(WriteData), .en(decoder_1_out24), .clk(clk), .Q(R24_q));  // open: clr
  Register #(.width(32)) R29 (.D(WriteData), .en(decoder_1_out29), .clk(clk), .Q(R29_q));  // open: clr
  Register #(.width(32)) R3 (.D(WriteData), .en(decoder_1_out3), .clk(clk), .Q(R3_q));  // open: clr
  Register #(.width(32)) R8 (.D(WriteData), .en(decoder_1_out8), .clk(clk), .Q(R8_q));  // open: clr
  Register #(.width(32)) R13 (.D(WriteData), .en(decoder_1_out13), .clk(clk), .Q(R13_q));  // open: clr
  Register #(.width(32)) R18 (.D(WriteData), .en(decoder_1_out18), .clk(clk), .Q(R18_q));  // open: clr
  Register #(.width(32)) R23 (.D(WriteData), .en(decoder_1_out23), .clk(clk), .Q(R23_q));  // open: clr
  Register #(.width(32)) R28 (.D(WriteData), .en(decoder_1_out28), .clk(clk), .Q(R28_q));  // open: clr
  Register #(.width(32)) R2 (.D(WriteData), .en(decoder_1_out2), .Q(R2_q));  // open: clk, clr
  Register #(.width(32)) R7 (.D(WriteData), .en(decoder_1_out7), .clk(clk), .Q(R7_q));  // open: clr
  Register #(.width(32)) R12 (.D(WriteData), .en(decoder_1_out12), .clk(clk), .Q(R12_q));  // open: clr
  Register #(.width(32)) R17 (.D(WriteData), .en(decoder_1_out17), .clk(clk), .Q(R17_q));  // open: clr
  Register #(.width(32)) R22 (.D(WriteData), .en(decoder_1_out22), .clk(clk), .Q(R22_q));  // open: clr
  Register #(.width(32)) R27 (.D(WriteData), .en(decoder_1_out27), .clk(clk), .Q(R27_q));  // open: clr
  Register #(.width(32)) R1 (.D(WriteData), .en(decoder_1_out1), .clk(clk), .Q(R1_q));  // open: clr
  Register #(.width(32)) R6 (.D(WriteData), .en(decoder_1_out6), .clk(clk), .Q(R6_q));  // open: clr
  Register #(.width(32)) R11 (.D(WriteData), .en(decoder_1_out11), .clk(clk), .Q(R11_q));  // open: clr
  Register #(.width(32)) R16 (.D(WriteData), .en(decoder_1_out16), .clk(clk), .Q(R16_q));  // open: clr
  Register #(.width(32)) R21 (.D(WriteData), .en(decoder_1_out21), .clk(clk), .Q(R21_q));  // open: clr
  Register #(.width(32)) R26 (.D(WriteData), .en(decoder_1_out26), .clk(clk), .Q(R26_q));  // open: clr
  Register #(.width(32)) R31 (.D(WriteData), .en(decoder_1_out31), .clk(clk), .Q(R31_q));  // open: clr
  Register #(.width(32)) R0 (.D(WriteData), .en(decoder_1_out0), .clk(clk), .Q(R0_q));  // open: clr
  Register #(.width(32)) R5 (.D(WriteData), .en(decoder_1_out5), .clk(clk), .Q(R5_q));  // open: clr
  Register #(.width(32)) R10 (.D(WriteData), .en(decoder_1_out10), .clk(clk), .Q(R10_q));  // open: clr
  Register #(.width(32)) R15 (.D(WriteData), .en(decoder_1_out15), .clk(clk), .Q(R15_q));  // open: clr
  Register #(.width(32)) R20 (.D(WriteData), .en(decoder_1_out20), .clk(clk), .Q(R20_q));  // open: clr
  Register #(.width(32)) R25 (.D(WriteData), .en(decoder_1_out25), .clk(clk), .Q(R25_q));  // open: clr
  Register #(.width(32)) R30 (.D(WriteData), .en(decoder_1_out30), .clk(clk), .Q(R30_q));  // open: clr
  Multiplexer #(.select(5), .width(32)) multiplexer_1 (
    .in0(R0_q), .in1(R1_q), .in2(R2_q), .in3(R3_q), .in4(R4_q), .in5(R5_q), .in6(R6_q), .in7(R7_q),
    .in8(R8_q), .in9(R9_q), .in10(R10_q), .in11(R11_q), .in12(R12_q), .in13(R13_q), .in14(R14_q),
    .in15(R15_q), .in16(R16_q), .in17(R17_q), .in18(R18_q), .in19(R19_q), .in20(R20_q), .in21(R21_q),
    .in22(R22_q), .in23(R23_q), .in24(R24_q), .in25(R25_q), .in26(R26_q), .in27(R27_q), .in28(R28_q),
    .in29(R29_q), .in30(R30_q), .in31(R31_q), .out(ReadData1), .sel(rs));
  Multiplexer #(.select(5), .width(32)) multiplexer_2 (
    .in0(R0_q), .in1(R1_q), .in2(R2_q), .in3(R3_q), .in4(R4_q), .in5(R5_q), .in6(R6_q), .in7(R7_q),
    .in8(R8_q), .in9(R9_q), .in10(R10_q), .in11(R11_q), .in12(R12_q), .in13(R13_q), .in14(R14_q),
    .in15(R15_q), .in16(R16_q), .in17(R17_q), .in18(R18_q), .in19(R19_q), .in20(R20_q), .in21(R21_q),
    .in22(R22_q), .in23(R23_q), .in24(R24_q), .in25(R25_q), .in26(R26_q), .in27(R27_q), .in28(R28_q),
    .in29(R29_q), .in30(R30_q), .in31(R31_q), .out(ReadData2), .sel(rt));
endmodule

module ID_EX (
  input  [31:0] pc_in,
  input  [31:0] RD1_in,
  input  [31:0] RD2_in,
  input  [31:0] Imm_in,
  input  stall,
  input  flush,
  input  [4:0] rs_in,
  input  [4:0] rt_in,
  input  [4:0] rd_in,
  input  regdst_in,
  input  ALUsrec_in,
  input  [1:0] ALUOp_in,
  input  Branch_in,
  input  clk,
  output [31:0] pc_out,
  output [31:0] RD1_out,
  output [31:0] RD2_out,
  output [31:0] Imm_out,
  output [4:0] rs_out,
  output [4:0] rt_out,
  output [4:0] rd_out,
  output REGDST_out,
  output ALUsrc_out,
  output [1:0] ALUOP_out,
  output Branch_out
);

  Register #(.width(1)) register_1 (.D(regdst_in), .en(stall), .clk(clk), .Q(REGDST_out), .clr(flush));
  Register #(.width(1)) register_2 (.D(ALUsrec_in), .en(stall), .clk(clk), .Q(ALUsrc_out), .clr(flush));
  Register #(.width(2)) register_3 (.D(ALUOp_in), .en(stall), .clk(clk), .Q(ALUOP_out), .clr(flush));
  Register #(.width(32)) register_4 (.D(pc_in), .en(stall), .clk(clk), .Q(pc_out), .clr(flush));
  Register #(.width(32)) register_5 (.D(RD1_in), .en(stall), .clk(clk), .Q(RD1_out), .clr(flush));
  Register #(.width(32)) register_6 (.D(RD2_in), .en(stall), .clk(clk), .Q(RD2_out), .clr(flush));
  Register #(.width(32)) register_7 (.D(Imm_in), .en(stall), .clk(clk), .Q(Imm_out), .clr(flush));
  Register #(.width(5)) register_8 (.D(rs_in), .en(stall), .clk(clk), .Q(rs_out), .clr(flush));
  Register #(.width(5)) register_9 (.D(rt_in), .en(stall), .clk(clk), .Q(rt_out), .clr(flush));
  Register #(.width(5)) register_10 (.D(rd_in), .en(stall), .clk(clk), .Q(rd_out), .clr(flush));
  Register #(.width(1)) register_11 (.D(Branch_in), .en(stall), .clk(clk), .Q(Branch_out), .clr(flush));
endmodule

module Control (
  input  [5:0] Opcode,
  output RegDst,
  output ALUSrc,
  output [1:0] ALUOp,
  output MemRead,
  output MemWrite,
  output MemToReg,
  output RegWrite,
  output Branch
);

  Comparator #(.width(6)) comparator_1 (.a(Opcode), .b({6{1'b0}}), .eq(ALUOp[1]));  // open: gt, lt
  Comparator #(.width(6)) comparator_2 (.a(Opcode), .b(6'b100011), .eq(MemRead));  // open: gt, lt
  Comparator #(.width(6)) comparator_3 (.a(Opcode), .b(6'b101011), .eq(MemWrite));  // open: gt, lt
  Comparator #(.width(6)) comparator_4 (.a(Opcode), .b(6'b000100), .eq(ALUOp[0]));  // open: gt, lt
  or or_1 (ALUSrc, MemRead, MemWrite);
  or or_2 (RegWrite, ALUOp[1], MemRead);

  assign Branch = ALUOp[0];
  assign MemToReg = MemRead;
  assign RegDst = ALUOp[1];
endmodule

module ALU (
  input  [31:0] A,
  input  [31:0] B,
  input  [3:0] ALUCtrl,
  output [31:0] Result,
  output Zero
);

  wire [31:0] adder_1_out, and_1_out, bit_extender_1_out, or_1_out, subtractor_1_out;

  assign and_1_out = A & B;  // AND_Gate and_1, 32 bits wide
  assign or_1_out = A | B;  // OR_Gate or_1, 32 bits wide
  Adder #(.width(32)) adder_1 (.a(A), .b(B), .out(adder_1_out));  // open: cin, cout
  Subtractor #(.width(32)) subtractor_1 (.a(A), .b(B), .out(subtractor_1_out));  // open: bin, bout
  Multiplexer #(.select(3), .width(32)) multiplexer_1 (
    .in2(and_1_out), .in3(or_1_out), .in4(adder_1_out), .in5(subtractor_1_out), .in6(bit_extender_1_out),
    .out(Result), .sel(ALUCtrl[2:0]));  // open: in0, in1, in7
  assign bit_extender_1_out = {{31{subtractor_1_out[31]}}, subtractor_1_out[31]};  // Bit_Extender bit_extender_1
  Comparator #(.width(32)) comparator_1 (.a({32{1'b0}}), .b(Result), .eq(Zero));  // open: gt, lt
endmodule

module EX_MEM (
  input  [31:0] ALUResult_EX,
  input  [31:0] WriteData_EX,
  input  BranchTaken_EX,
  input  MemRead_EX,
  input  MemWrite_EX,
  input  MemToReg_EX,
  input  RegWrite_EX,
  input  [31:0] BranchTarget_EX,
  input  [4:0] WriteReg_EX,
  input  reset,
  input  clk,
  output [31:0] ALUResult_EXMEM,
  output [31:0] WriteData_EXMEM,
  output BranchTaken_EXMEM,
  output MemRead_EXMEM,
  output MemWrite_EXMEM,
  output MemToReg_EXMEM,
  output RegWrite_EXMEM,
  output [31:0] BranchTarget_EXMEM,
  output [4:0] WriteReg_EXMEM
);

  Register #(.width(32)) register_1 (.D(ALUResult_EX), .en(1'b1), .clk(clk), .Q(ALUResult_EXMEM), .clr(reset));
  Register #(.width(32)) register_2 (.D(WriteData_EX), .en(1'b1), .clk(clk), .Q(WriteData_EXMEM), .clr(reset));
  Register #(.width(1)) register_3 (.D(BranchTaken_EX), .en(1'b1), .clk(clk), .Q(BranchTaken_EXMEM), .clr(reset));
  Register #(.width(1)) register_4 (.D(MemRead_EX), .en(1'b1), .clk(clk), .Q(MemRead_EXMEM), .clr(reset));
  Register #(.width(1)) register_5 (.D(MemWrite_EX), .en(1'b1), .clk(clk), .Q(MemWrite_EXMEM), .clr(reset));
  Register #(.width(1)) register_6 (.D(MemToReg_EX), .en(1'b1), .clk(clk), .Q(MemToReg_EXMEM), .clr(reset));
  Register #(.width(1)) register_7 (.D(RegWrite_EX), .en(1'b1), .clk(clk), .Q(RegWrite_EXMEM), .clr(reset));
  Register #(.width(32)) register_8 (.D(BranchTarget_EX), .en(1'b1), .clk(clk), .Q(BranchTarget_EXMEM), .clr(reset));
  Register #(.width(5)) register_9 (.D(WriteReg_EX), .en(1'b1), .clk(clk), .Q(WriteReg_EXMEM), .clr(reset));
endmodule

module MEM_WB (
  input  [31:0] ReadData_in,
  input  [31:0] ALUResult_in,
  input  [4:0] WriteReg_in,
  input  RegWrite_in,
  input  MemToReg_in,
  input  reset,
  input  clk,
  output [31:0] ReadData_out,
  output [31:0] ALUResult_out,
  output [4:0] WriteReg_out,
  output RegWrite_out,
  output MemToReg_out
);

  Register #(.width(32)) register_1 (.D(ReadData_in), .en(1'b1), .clk(clk), .Q(ReadData_out), .clr(reset));
  Register #(.width(32)) register_2 (.D(ALUResult_in), .en(1'b1), .clk(clk), .Q(ALUResult_out), .clr(reset));
  Register #(.width(5)) register_3 (.D(WriteReg_in), .en(1'b1), .clk(clk), .Q(WriteReg_out), .clr(reset));
  Register #(.width(1)) register_4 (.D(RegWrite_in), .en(1'b1), .clk(clk), .Q(RegWrite_out), .clr(reset));
  Register #(.width(1)) register_5 (.D(MemToReg_in), .en(1'b1), .clk(clk), .Q(MemToReg_out), .clr(reset));
endmodule
